# Fritzing sketch FdS Multiplex Wing (saved by Fritzing 0.9.3b)
circuit board: 5.08cm x 2.3cm
breadboards: 1

parts:
  Composant1 = Adafruit FeatherWing Proto [part_number="Adafruit #2884"]  # not connected
  100k = Resistor [tolerance=±5% resistance=220 package=THT]
  100k_2 = Resistor [tolerance=±5% resistance=100k package=THT]
  2x100k = Resistor [tolerance=±5% resistance=220 package=THT]
  2x100k_2 = Resistor [tolerance=±5% resistance=220 package=THT]
  CD4051BE = IC, DIP package, 16 pins [chip_label=CD4051BE]
  R1 = Resistor [tolerance=±5% resistance=220 package=THT]
  R2 = Resistor [tolerance=±5% resistance=220 package=THT]
  R3 = Resistor [tolerance=±5% resistance=220 package=THT]
  R4 = Resistor [tolerance=±5% resistance=220 package=THT]
  R5 = Resistor [tolerance=±5% resistance=220 package=THT]
  R6 = Resistor [tolerance=±5% resistance=220 package=THT]

nets:
  N1: 100k.Pin_0, 2x100k.Pin_0, CD4051BE.pin13
  N2: 100k_2.Pin_0, 2x100k_2.Pin_0, CD4051BE.pin14
  N3: 2x100k.Pin_1, CD4051BE.pin6, CD4051BE.pin7, CD4051BE.pin8
  N4: CD4051BE.pin2, R5.Pin_1
  N5: CD4051BE.pin4, R6.Pin_1
  N6: CD4051BE.pin16, R1.Pin_0, R2.Pin_0, R3.Pin_0, R4.Pin_0, R5.Pin_0, R6.Pin_0

notes:
  Reset
  GND
  3v3
  3
  5
  4
  6
  7
  2
  A1
  A2
  A3
  SCL
  SDA
  VUSB:0
  VBat:1
  2022
  Feather Wing
  Daron
  Multiplex 4 audio
  ST
  A0 COM
  A
  B
  C
  A4
  A5
  RX
  TX
  5v
  Relier les boutons actifs avec des résistances 10k-100k au 3v3 ici à coté pour en faire des pullups.
  Les switch des Rotary Encoders (5, 6, 7) peuvent avoir un pullup séparé.
  Deux ponts diviseurs pour mesurer la tension batterie et USB.
  Attention le bouton 7 est dans un trou unique avec son pullup.
  A1 pour volume
  Les rotarys sont à relier sur
  A2 A3 = A B
  A4 A5 = A B
  RX TX = A B
  En

custom parts:
  Adafruit FeatherWing Proto: This is the FeatherWing Proto - a prototyping add-on for all Feather boards. Using our Feather Stacking Headers or Feather Female Headers you can connect a FeatherWing on top or bottom of your Feather board and let the board take flight! This has a duplicate breakout for each pin on a Feather, as well as a bunch of plain grid proto holes. For GND and 3.3V, we give you a strip of connected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
